// Logisim project washing_pipeline.circ as structural Verilog: 24 circuits, main circuit washing_pipeline
module full_adder (
  input  a,
  input  b,
  input  cin,
  output s,
  output cout
);

  wire g, p, pc;

  xor xor_1 (p, a, b);
  xor xor_2 (s, p, cin);
  and and_1 (g, a, b);
  and and_2 (pc, p, cin);
  or or_1 (cout, g, pc);

  // Notes on the sheet:
  //   1-bit full adder
endmodule

module add8 (
  input  [7:0] a,
  input  [7:0] b,
  input  cin,
  output [7:0] s,
  output cout
);

  wire c1, c2, c3, c4, c5, c6, c7;

  full_adder fa4 (.a(a[4]), .b(b[4]), .cin(c4), .s(s[4]), .cout(c5));
  full_adder fa5 (.a(a[5]), .b(b[5]), .cin(c5), .s(s[5]), .cout(c6));
  full_adder fa0 (.a(a[0]), .b(b[0]), .cin(cin), .s(s[0]), .cout(c1));
  full_adder fa6 (.a(a[6]), .b(b[6]), .cin(c6), .s(s[6]), .cout(c7));
  full_adder fa1 (.a(a[1]), .b(b[1]), .cin(c1), .s(s[1]), .cout(c2));
  full_adder fa7 (.a(a[7]), .b(b[7]), .cin(c7), .s(s[7]), .cout(cout));
  full_adder fa2 (.a(a[2]), .b(b[2]), .cin(c2), .s(s[2]), .cout(c3));
  full_adder fa3 (.a(a[3]), .b(b[3]), .cin(c3), .s(s[3]), .cout(c4));

  // Notes on the sheet:
  //   8-bit ripple-carry adder: s = a + b + cin, cout
  //   fa4  (full_adder)
  //   fa5  (full_adder)
  //   fa0  (full_adder)
  //   fa6  (full_adder)
  //   fa1  (full_adder)
  //   fa7  (full_adder)
  //   fa2  (full_adder)
  //   fa3  (full_adder)
endmodule

module mux2_8 (
  input  sel,
  input  [7:0] a,
  input  [7:0] b,
  output [7:0] y
);

  wire nsel;
  wire [7:0] a_g, b_g;

  not not_1 (nsel, sel);
  assign a_g = a & {8{nsel}};  // AND_Gate and_1, 8 bits wide
  assign b_g = b & {8{sel}};  // AND_Gate and_2, 8 bits wide
  assign y = a_g | b_g;  // OR_Gate or_1, 8 bits wide

  // Other names for the same wires on the sheet: nsel8[7:0] = {8{nsel}}; sel8[7:0] = {8{sel}}

  // Notes on the sheet:
  //   8-bit 2:1 multiplexer  y = sel ? b : a
endmodule

module fetch (
  input  clk,
  input  rst,
  input  redirect,
  input  [7:0] target,
  input  stall,
  input  haltEX,
  output [7:0] pc,
  output [15:0] ir,
  output halted
);

  wire halted_d, pc_cy, pc_en, run;
  wire [7:0] pc_next, pc_plus1;

  Register register_1 (.D(pc_next), .en(pc_en), .Q(pc), .clk(clk), .clr(rst));
  or or_1 (halted_d, halted, haltEX);
  add8 pc_inc (.a(pc), .b({8{1'b0}}), .cin(1'b1), .s(pc_plus1), .cout(pc_cy));
  Register #(.width(1)) register_2 (.D(halted_d), .en(1'b1), .Q(halted), .clk(clk), .clr(rst));
  ROM #(.dataWidth(16)) rom_1 (.addr(pc), .data(ir));
  mux2_8 pc_mux (.sel(redirect), .a(pc_plus1), .b(target), .y(pc_next));
  nor nor_1 (run, stall, halted, haltEX);
  or or_2 (pc_en, redirect, run);

  // Notes on the sheet:
  //   IF stage: PC, +1 incrementer, next-PC mux, instruction ROM, HALT flag
  //   pc_inc  (add8)
  //   contents of rom_1 (hex, n*v repeats v):
  //   1cf4 1000 7180 1cf5 1001 7180 1cf8 1000 7180 1cf7 1000 7180 1cf0 6380 1009 5040 1409 4080 a00c 1002
  //   5200 a21a 1664 180a 1a0c b01d 1696 180f 1a14 1cf4 1020 7180 1cf5 1002 7180 1cf4 1021 7180 1cf1 6580
  //   d4c0 a426 1cf4 1020 7180 1cf5 1003 7180 1e04 1224 1cf4 7380 1cf7 7980 1cf8 1003 7180 1cf9 6180 9039
  //   1024 4040 9041 1224 b042 122c 8eff ae32 1cf4 1020 7180 1cf5 1004 7180 1cf4 1030 7180 1cf1 6580 100a
  //   d080 a04d 1cf5 1005 7180 1cf7 7b80 1cf8 1003 7180 1cf4 1034 7180 1cf9 6180 905d 1cf4 1020 7180 1cf4
  //   1040 7180 1cf5 10d0 7180 c000
  //   pc_mux  (mux2_8)
endmodule

module ifid (
  input  clk,
  input  rst,
  input  hold,
  input  flush,
  input  halted,
  input  [15:0] ir_in,
  output v,
  output [15:0] ir
);

  wire run, v_d;

  not not_1 (run, hold);
  nor nor_1 (v_d, flush, halted);
  Register #(.width(1)) register_1 (.D(v_d), .en(run), .Q(v), .clk(clk), .clr(rst));
  Register #(.width(16)) register_2 (.D(ir_in), .en(run), .Q(ir), .clk(clk), .clr(rst));

  // Notes on the sheet:
  //   IF/ID register: valid bit + instruction word
endmodule

module decode (
  input  [15:0] ir,
  output regWrite,
  output memRead,
  output memWrite,
  output aluSrcImm,
  output brZ,
  output brNZ,
  output jmp,
  output halt,
  output usesA,
  output usesB,
  output [2:0] aluOp,
  output [2:0] fA,
  output [2:0] fB,
  output [7:0] imm
);

  wire isADD, isADDI, isAND, isBEQZ, isBNEZ, isHALT, isJMP, isLD, isLDI, isMOV, isSLTU, isST, isSUB, no0,
       no1, no2, no3;

  buf buffer_1 (aluOp[2], isSLTU);
  and and_1 (isMOV, no3, no2, ir[13], no0);
  and and_2 (isADDI, ir[15], no2, no1, no0);
  or or_1 (usesB, isMOV, isADD, isSUB, isAND, isSLTU, isLD, isST);
  or or_2 (regWrite, isLDI, isMOV, isADD, isSUB, isAND, isLD, isADDI, isSLTU);
  and and_3 (isADD, no3, no2, ir[13], ir[12]);
  and and_4 (isBEQZ, ir[15], no2, no1, ir[12]);
  buf buffer_2 (memRead, isLD);
  not not_1 (no0, ir[12]);
  and and_5 (isSUB, no3, ir[14], no1, no0);
  and and_6 (isBNEZ, ir[15], no2, ir[13], no0);
  buf buffer_3 (memWrite, isST);
  buf buffer_4 (brZ, isBEQZ);
  not not_2 (no1, ir[13]);
  buf buffer_5 (brNZ, isBNEZ);
  and and_7 (isAND, no3, ir[14], no1, ir[12]);
  or or_3 (aluSrcImm, isLDI, isADDI);
  not not_3 (no2, ir[14]);
  and and_8 (isJMP, ir[15], no2, ir[13], ir[12]);
  buf buffer_6 (jmp, isJMP);
  not not_4 (no3, ir[15]);
  and and_9 (isLD, no3, ir[14], ir[13], no0);
  and and_10 (isHALT, ir[15], ir[14], no1, no0);
  or or_4 (aluOp[0], isADD, isADDI, isAND);
  buf buffer_7 (halt, isHALT);
  and and_11 (isLDI, no3, no2, no1, ir[12]);
  and and_12 (isST, no3, ir[14], ir[13], ir[12]);
  and and_13 (isSLTU, ir[15], ir[14], no1, ir[12]);
  or or_5 (aluOp[1], isSUB, isAND);
  or or_6 (usesA, isADD, isSUB, isAND, isSLTU, isADDI, isST, isBEQZ, isBNEZ);

  assign fA = ir[11:9];
  assign fB = ir[8:6];
  assign imm = ir[7:0];

  // Other names for the same wires on the sheet: o0 = ir[12]; op[3:0] = ir[15:12]; o1 = ir[13]; o2 = ir[14];
  //   o3 = ir[15]

  // Notes on the sheet:
  //   ID stage: instruction fields and control word
endmodule

module dec3 (
  input  [2:0] a,
  input  en,
  output [7:0] y
);

  wire n0, n1, n2;

  and and_1 (y[4], en, n0, n1, a[2]);
  not not_1 (n0, a[0]);
  and and_2 (y[5], en, a[0], n1, a[2]);
  not not_2 (n1, a[1]);
  not not_3 (n2, a[2]);
  and and_3 (y[6], en, n0, a[1], a[2]);
  and and_4 (y[7], en, a[0], a[1], a[2]);
  and and_5 (y[0], en, n0, n1, n2);
  and and_6 (y[1], en, a[0], n1, n2);
  and and_7 (y[2], en, n0, a[1], n2);
  and and_8 (y[3], en, a[0], a[1], n2);

  // Notes on the sheet:
  //   3-to-8 decoder with enable: y[i] = en & (a == i)
endmodule

module mux8_8 (
  input  [2:0] s,
  input  [7:0] d0,
  input  [7:0] d1,
  input  [7:0] d2,
  input  [7:0] d3,
  input  [7:0] d4,
  input  [7:0] d5,
  input  [7:0] d6,
  input  [7:0] d7,
  output [7:0] y
);

  wire [7:0] l0_0, l0_1, l0_2, l0_3, l1_0, l1_1;

  mux2_8 m2 (.sel(s[2]), .a(l1_0), .b(l1_1), .y(y));
  mux2_8 m0_0 (.sel(s[0]), .a(d0), .b(d1), .y(l0_0));
  mux2_8 m0_1 (.sel(s[0]), .a(d2), .b(d3), .y(l0_1));
  mux2_8 m0_2 (.sel(s[0]), .a(d4), .b(d5), .y(l0_2));
  mux2_8 m0_3 (.sel(s[0]), .a(d6), .b(d7), .y(l0_3));
  mux2_8 m1_0 (.sel(s[1]), .a(l0_0), .b(l0_1), .y(l1_0));
  mux2_8 m1_1 (.sel(s[1]), .a(l0_2), .b(l0_3), .y(l1_1));

  // Notes on the sheet:
  //   8-bit 8:1 multiplexer built from 7 x mux2_8
  //   m2  (mux2_8)
  //   m0_0  (mux2_8)
  //   m0_1  (mux2_8)
  //   m0_2  (mux2_8)
  //   m0_3  (mux2_8)
  //   m1_0  (mux2_8)
  //   m1_1  (mux2_8)
endmodule

module eq3 (
  input  [2:0] a,
  input  [2:0] b,
  output eq
);

  wire [2:0] d;

  assign d = a ^ b;  // XOR_Gate xor_1, 3 bits wide
  nor nor_1 (eq, d[0], d[1], d[2]);

  // Notes on the sheet:
  //   eq = 1 when 3-bit a == b
endmodule

module regfile (
  input  clk,
  input  [2:0] raA,
  input  [2:0] raB,
  input  wEn,
  input  [2:0] wAddr,
  input  [7:0] wData,
  output [7:0] rdA,
  output [7:0] rdB
);

  wire bypA, bypB, sameA, sameB, ws0, ws1, ws2, ws3, ws4, ws5, ws6, ws7;
  wire [7:0] r0, r1, r2, r3, r4, r5, r6, r7, rawA, rawB;

  Register register_1 (.D(wData), .en(ws4), .Q(r4), .clk(clk), .clr(1'b0));
  and and_1 (bypA, sameA, wEn);
  dec3 wdec (.a(wAddr), .en(wEn), .y({ws7, ws6, ws5, ws4, ws3, ws2, ws1, ws0}));
  mux2_8 bypmuxA (.sel(bypA), .a(rawA), .b(wData), .y(rdA));
  Register register_2 (.D(wData), .en(ws5), .Q(r5), .clk(clk), .clr(1'b0));
  mux8_8 rdB_i (.s(raB), .d0(r0), .d1(r1), .d2(r2), .d3(r3), .d4(r4), .d5(r5), .d6(r6), .d7(r7), .y(rawB));
  Register register_3 (.D(wData), .en(ws6), .Q(r6), .clk(clk), .clr(1'b0));
  Register register_4 (.D(wData), .en(ws0), .Q(r0), .clk(clk), .clr(1'b0));
  eq3 cmpB (.a(raB), .b(wAddr), .eq(sameB));
  Register register_5 (.D(wData), .en(ws7), .Q(r7), .clk(clk), .clr(1'b0));
  Register register_6 (.D(wData), .en(ws1), .Q(r1), .clk(clk), .clr(1'b0));
  and and_2 (bypB, sameB, wEn);
  mux8_8 rdA_i (.s(raA), .d0(r0), .d1(r1), .d2(r2), .d3(r3), .d4(r4), .d5(r5), .d6(r6), .d7(r7), .y(rawA));
  Register register_7 (.D(wData), .en(ws2), .Q(r2), .clk(clk), .clr(1'b0));
  mux2_8 bypmuxB (.sel(bypB), .a(rawB), .b(wData), .y(rdB));
  eq3 cmpA (.a(raA), .b(wAddr), .eq(sameA));
  Register register_8 (.D(wData), .en(ws3), .Q(r3), .clk(clk), .clr(1'b0));

  // Other names for the same wires on the sheet: wsel[7:0] = {ws7, ws6, ws5, ws4, ws3, ws2, ws1, ws0}

  // Notes on the sheet:
  //   Register file R0-R7 (WB write bypassed to ID reads)
  //   wdec  (dec3)
  //   bypmuxA  (mux2_8)
  //   rdB_i  (mux8_8)
  //   cmpB  (eq3)
  //   rdA_i  (mux8_8)
  //   bypmuxB  (mux2_8)
  //   cmpA  (eq3)
endmodule

module idex (
  input  clk,
  input  rst,
  input  vnext,
  input  regWrite_d,
  input  memRead_d,
  input  memWrite_d,
  input  aluSrcImm_d,
  input  brZ_d,
  input  brNZ_d,
  input  jmp_d,
  input  halt_d,
  input  usesA_d,
  input  usesB_d,
  input  [2:0] aluOp_d,
  input  [2:0] fA_d,
  input  [2:0] fB_d,
  input  [7:0] imm_d,
  input  [7:0] aval_d,
  input  [7:0] bval_d,
  output regWrite,
  output memRead,
  output memWrite,
  output aluSrcImm,
  output brZ,
  output brNZ,
  output jmp,
  output halt,
  output usesA,
  output usesB,
  output [2:0] aluOp,
  output [2:0] fA,
  output [2:0] fB,
  output [7:0] imm,
  output [7:0] aval,
  output [7:0] bval,
  output v
);

  Register #(.width(3)) register_1 (.D(fA_d), .en(1'b1), .Q(fA), .clk(clk), .clr(rst));
  Register #(.width(1)) register_2 (.D(brNZ_d), .en(1'b1), .Q(brNZ), .clk(clk), .clr(rst));
  Register #(.width(1)) register_3 (.D(regWrite_d), .en(1'b1), .Q(regWrite), .clk(clk), .clr(rst));
  Register #(.width(3)) register_4 (.D(fB_d), .en(1'b1), .Q(fB), .clk(clk), .clr(rst));
  Register #(.width(1)) register_5 (.D(jmp_d), .en(1'b1), .Q(jmp), .clk(clk), .clr(rst));
  Register #(.width(1)) register_6 (.D(memRead_d), .en(1'b1), .Q(memRead), .clk(clk), .clr(rst));
  Register #(.width(1)) register_7 (.D(halt_d), .en(1'b1), .Q(halt), .clk(clk), .clr(rst));
  Register register_8 (.D(imm_d), .en(1'b1), .Q(imm), .clk(clk), .clr(rst));
  Register #(.width(1)) register_9 (.D(memWrite_d), .en(1'b1), .Q(memWrite), .clk(clk), .clr(rst));
  Register register_10 (.D(aval_d), .en(1'b1), .Q(aval), .clk(clk), .clr(rst));
  Register #(.width(1)) register_11 (.D(usesA_d), .en(1'b1), .Q(usesA), .clk(clk), .clr(rst));
  Register register_12 (.D(bval_d), .en(1'b1), .Q(bval), .clk(clk), .clr(rst));
  Register #(.width(1)) register_13 (.D(usesB_d), .en(1'b1), .Q(usesB), .clk(clk), .clr(rst));
  Register #(.width(1)) register_14 (.D(aluSrcImm_d), .en(1'b1), .Q(aluSrcImm), .clk(clk), .clr(rst));
  Register #(.width(1)) register_15 (.D(vnext), .en(1'b1), .Q(v), .clk(clk), .clr(rst));
  Register #(.width(1)) register_16 (.D(brZ_d), .en(1'b1), .Q(brZ), .clk(clk), .clr(rst));
  Register #(.width(3)) register_17 (.D(aluOp_d), .en(1'b1), .Q(aluOp), .clk(clk), .clr(rst));

  // Notes on the sheet:
  //   ID/EX register
endmodule

module hazard (
  input  idexV,
  input  idexMemRead,
  input  ifidV,
  input  usesA,
  input  usesB,
  input  redirect,
  input  haltEX,
  input  [2:0] idexDest,
  input  [2:0] fA,
  input  [2:0] fB,
  output stall,
  output kill,
  output vnext
);

  wire eqA, eqB, hit, hitA, hitB, loadUse, nkill, nstall;

  or or_1 (kill, redirect, haltEX);
  eq3 cA (.a(fA), .b(idexDest), .eq(eqA));
  not not_1 (nkill, kill);
  eq3 cB (.a(fB), .b(idexDest), .eq(eqB));
  and and_1 (stall, loadUse, nkill);
  and and_2 (hitA, eqA, usesA);
  not not_2 (nstall, stall);
  and and_3 (hitB, eqB, usesB);
  and and_4 (vnext, ifidV, nkill, nstall);
  or or_2 (hit, hitA, hitB);
  and and_5 (loadUse, idexV, idexMemRead, ifidV, hit);

  // Notes on the sheet:
  //   Load-use stall, flush priority and ID/EX valid-next
  //   cA  (eq3)
  //   cB  (eq3)
endmodule

module fwd (
  input  [2:0] f,
  input  uses,
  input  [7:0] val,
  input  exV,
  input  exRW,
  input  exMR,
  input  [2:0] exDest,
  input  [7:0] exAlu,
  input  wbV,
  input  wbRW,
  input  [2:0] wbDest,
  input  [7:0] wbData,
  output [7:0] y
);

  wire eqEx, eqWb, exNL, hitEx, hitWb, hitWb0, nhitEx, none;
  wire [7:0] tEx, tId, tWb;

  and and_1 (hitWb, hitWb0, nhitEx);
  assign tId = val & {8{none}};  // AND_Gate and_2, 8 bits wide
  eq3 cEx (.a(f), .b(exDest), .eq(eqEx));
  nor nor_1 (none, hitEx, hitWb);
  assign y = tEx | tWb | tId;  // OR_Gate or_1, 8 bits wide
  eq3 cWb (.a(f), .b(wbDest), .eq(eqWb));
  not not_1 (exNL, exMR);
  and and_3 (hitEx, uses, exV, exRW, exNL, eqEx);
  and and_4 (hitWb0, uses, wbV, wbRW, eqWb);
  not not_2 (nhitEx, hitEx);
  assign tEx = exAlu & {8{hitEx}};  // AND_Gate and_5, 8 bits wide
  assign tWb = wbData & {8{hitWb}};  // AND_Gate and_6, 8 bits wide

  // Other names for the same wires on the sheet: hitEx8[7:0] = {8{hitEx}}; hitWb8[7:0] = {8{hitWb}};
  //   none8[7:0] = {8{none}}

  // Notes on the sheet:
  //   Forwarding mux: EX/MEM (youngest) > MEM/WB > ID/EX value
  //   cEx  (eq3)
  //   cWb  (eq3)
endmodule

module alu (
  input  [7:0] a,
  input  [7:0] b,
  input  [2:0] op,
  output [7:0] y
);

  wire borrow, cout, is_add, is_and, is_pass, is_sltu, is_sub, is_sum, no0, no1, no2, sub;
  wire [7:0] and_r, bx, r_and, r_pass, r_sltu, r_sum, sum;

  not not_1 (borrow, cout);
  and and_1 (is_and, no2, op[1], op[0]);
  assign and_r = a & b;  // AND_Gate and_2, 8 bits wide
  not not_2 (no0, op[0]);
  and and_3 (is_sltu, op[2], no1, no0);
  not not_3 (no1, op[1]);
  assign r_pass = b & {8{is_pass}};  // AND_Gate and_4, 8 bits wide
  not not_4 (no2, op[2]);
  or or_1 (sub, is_sub, is_sltu);
  assign r_sum = sum & {8{is_sum}};  // AND_Gate and_5, 8 bits wide
  and and_6 (is_pass, no2, no1, no0);
  or or_2 (is_sum, is_add, is_sub);
  assign r_and = and_r & {8{is_and}};  // AND_Gate and_7, 8 bits wide
  and and_8 (is_add, no2, no1, op[0]);
  assign r_sltu = {{7{1'b0}}, borrow} & {8{is_sltu}};  // AND_Gate and_9, 8 bits wide
  assign bx = b ^ {8{sub}};  // XOR_Gate xor_1, 8 bits wide
  and and_10 (is_sub, no2, op[1], no0);
  assign y = r_pass | r_sum | r_and | r_sltu;  // OR_Gate or_3, 8 bits wide
  add8 adder (.a(a), .b(bx), .cin(sub), .s(sum), .cout(cout));

  // Other names for the same wires on the sheet: is_and8[7:0] = {8{is_and}}; is_pass8[7:0] = {8{is_pass}};
  //   is_sltu8[7:0] = {8{is_sltu}}; is_sum8[7:0] = {8{is_sum}}; o0 = op[0]; o1 = op[1]; o2 = op[2];
  //   sltu_r[0] = borrow; sub8[7:0] = {8{sub}}

  // Notes on the sheet:
  //   ALU: op 0 PASSB, 1 ADD, 2 SUB, 3 AND, 4 SLTU
  //   adder  (add8)
endmodule

module zero8 (
  input  [7:0] a,
  output z
);

  nor nor_1 (z, a[0], a[1], a[2], a[3], a[4], a[5], a[6], a[7]);

  // Notes on the sheet:
  //   z = 1 when the 8-bit input is zero
endmodule

module execute (
  input  [7:0] aval,
  input  [7:0] bval,
  input  [7:0] imm,
  input  [2:0] fA,
  input  [2:0] fB,
  input  [2:0] aluOp,
  input  usesA,
  input  usesB,
  input  aluSrcImm,
  input  brZ,
  input  brNZ,
  input  jmp,
  input  halt,
  input  v,
  input  exV,
  input  exRW,
  input  exMR,
  input  [2:0] exDest,
  input  [7:0] exAlu,
  input  wbV,
  input  wbRW,
  input  [2:0] wbDest,
  input  [7:0] wbData,
  output [7:0] alu_out,
  output [7:0] fwdA,
  output redirect,
  output haltEX
);

  wire isZero, notZero, take, takeNZ, takeZ;
  wire [7:0] fwdB, opb;

  and and_1 (takeZ, brZ, isZero);
  fwd fwdA_u (
    .f(fA), .uses(usesA), .val(aval), .exV(exV), .exRW(exRW), .exMR(exMR), .exDest(exDest), .exAlu(exAlu),
    .wbV(wbV), .wbRW(wbRW), .wbDest(wbDest), .wbData(wbData), .y(fwdA));
  and and_2 (takeNZ, brNZ, notZero);
  fwd fwdB_u (
    .f(fB), .uses(usesB), .val(bval), .exV(exV), .exRW(exRW), .exMR(exMR), .exDest(exDest), .exAlu(exAlu),
    .wbV(wbV), .wbRW(wbRW), .wbDest(wbDest), .wbData(wbData), .y(fwdB));
  or or_1 (take, jmp, takeZ, takeNZ);
  mux2_8 opb_i (.sel(aluSrcImm), .a(fwdB), .b(imm), .y(opb));
  and and_3 (redirect, v, take);
  alu alu_u (.a(fwdA), .b(opb), .op(aluOp), .y(alu_out));
  and and_4 (haltEX, v, halt);
  zero8 ztest (.a(fwdA), .z(isZero));
  not not_1 (notZero, isZero);

  // Notes on the sheet:
  //   EX stage: forwarding, ALU, branch/jump/HALT resolution
  //   fwdA_u  (fwd)
  //   fwdB_u  (fwd)
  //   opb_i  (mux2_8)
  //   alu_u  (alu)
  //   ztest  (zero8)
endmodule

module exmem (
  input  clk,
  input  rst,
  input  v_d,
  input  regWrite_d,
  input  memRead_d,
  input  memWrite_d,
  input  [2:0] dest_d,
  input  [7:0] alu_d,
  input  [7:0] stData_d,
  output v,
  output regWrite,
  output memRead,
  output memWrite,
  output [2:0] dest,
  output [7:0] alu,
  output [7:0] stData
);

  Register register_1 (.D(alu_d), .en(1'b1), .Q(alu), .clk(clk), .clr(rst));
  Register #(.width(1)) register_2 (.D(v_d), .en(1'b1), .Q(v), .clk(clk), .clr(rst));
  Register register_3 (.D(stData_d), .en(1'b1), .Q(stData), .clk(clk), .clr(rst));
  Register #(.width(1)) register_4 (.D(regWrite_d), .en(1'b1), .Q(regWrite), .clk(clk), .clr(rst));
  Register #(.width(1)) register_5 (.D(memRead_d), .en(1'b1), .Q(memRead), .clk(clk), .clr(rst));
  Register #(.width(1)) register_6 (.D(memWrite_d), .en(1'b1), .Q(memWrite), .clk(clk), .clr(rst));
  Register #(.width(3)) register_7 (.D(dest_d), .en(1'b1), .Q(dest), .clk(clk), .clr(rst));

  // Other names for the same wires on the sheet: alu_n[7:0] = alu

  // Notes on the sheet:
  //   EX/MEM register
endmodule

module mem_stage (
  input  v,
  input  memRead,
  input  memWrite,
  input  [7:0] addr,
  input  [7:0] wdata,
  input  clk,
  input  [7:0] rd_in_ctrl,
  input  [7:0] rd_water,
  input  [7:0] rd_temp,
  input  [7:0] rd_rpm,
  input  [7:0] rd_act,
  input  [7:0] rd_disp,
  input  [7:0] rd_tcount,
  input  [7:0] rd_tlimit,
  input  [7:0] rd_tctl,
  input  [7:0] rd_tstat,
  output [7:0] rdata,
  output wr_act,
  output wr_disp,
  output wr_tlim,
  output wr_tctl
);

  wire isPer, na0, na1, na2, na3, ram_q_oe, ramSel, sel0, sel1, sel2, sel3, sel4, sel5, sel6, sel7, sel8,
       sel9, storing, we_ram;
  wire [7:0] o1, o2, o3, ram_q, t_act, t_disp, t_in_ctrl, t_ram, t_rpm, t_tcount, t_tctl, t_temp, t_tlimit,
       t_tstat, t_water;

  and and_1 (storing, v, memWrite);
  and and_2 (wr_tlim, storing, sel7);
  and and_3 (sel0, isPer, na0, na1, na2, na3);
  and and_4 (sel6, isPer, na0, addr[1], addr[2], na3);
  assign o1 = t_ram | t_in_ctrl | t_water | t_temp;  // OR_Gate or_1, 8 bits wide
  and and_5 (sel1, isPer, addr[0], na1, na2, na3);
  and and_6 (sel7, isPer, addr[0], addr[1], addr[2], na3);
  and and_7 (wr_tctl, storing, sel8);
  assign t_water = rd_water & {8{sel1}};  // AND_Gate and_8, 8 bits wide
  assign t_act = rd_act & {8{sel4}};  // AND_Gate and_9, 8 bits wide
  assign t_tlimit = rd_tlimit & {8{sel7}};  // AND_Gate and_10, 8 bits wide
  not not_1 (ramSel, addr[7]);
  and and_11 (we_ram, storing, ramSel);
  assign o2 = t_rpm | t_act | t_disp | t_tcount;  // OR_Gate or_2, 8 bits wide
  and and_12 (sel2, isPer, na0, addr[1], na2, na3);
  and and_13 (sel8, isPer, na0, na1, na2, addr[3]);
  and and_14 (isPer, addr[7], addr[6], addr[5], addr[4]);
  not not_2 (na0, addr[0]);
  RAM #(.addrWidth(7), .asyncread("true"), .databus("bidir")) ram_1 (
    .addr(addr[6:0]), .we(we_ram), .oe(ram_q_oe), .clk(clk));  // open: data
  assign t_temp = rd_temp & {8{sel2}};  // AND_Gate and_15, 8 bits wide
  assign t_disp = rd_disp & {8{sel5}};  // AND_Gate and_16, 8 bits wide
  assign t_tctl = rd_tctl & {8{sel8}};  // AND_Gate and_17, 8 bits wide
  assign o3 = t_tlimit | t_tctl | t_tstat;  // OR_Gate or_3, 8 bits wide
  and and_18 (sel3, isPer, addr[0], addr[1], na2, na3);
  and and_19 (sel9, isPer, addr[0], na1, na2, addr[3]);
  assign t_ram = ram_q & {8{ramSel}};  // AND_Gate and_20, 8 bits wide
  not not_3 (na1, addr[1]);
  assign rdata = o1 | o2 | o3;  // OR_Gate or_4, 8 bits wide
  and and_21 (wr_act, storing, sel4);
  not not_4 (na2, addr[2]);
  and and_22 (sel4, isPer, na0, na1, addr[2], na3);
  assign ram_q = we_ram ? wdata : 8'bz;  // Controlled_Buffer controlled_buffer_1
  not not_5 (na3, addr[3]);
  and and_23 (wr_disp, storing, sel5);
  assign t_tcount = rd_tcount & {8{sel6}};  // AND_Gate and_24, 8 bits wide
  and and_25 (sel5, isPer, addr[0], na1, addr[2], na3);
  assign t_in_ctrl = rd_in_ctrl & {8{sel0}};  // AND_Gate and_26, 8 bits wide
  assign t_rpm = rd_rpm & {8{sel3}};  // AND_Gate and_27, 8 bits wide
  assign t_tstat = rd_tstat & {8{sel9}};  // AND_Gate and_28, 8 bits wide
  not not_6 (ram_q_oe, we_ram);

  // Other names for the same wires on the sheet: a0 = addr[0]; ramAddr[6:0] = addr[6:0]; a1 = addr[1]; a2 = addr[2];
  //   a3 = addr[3]; a4 = addr[4]; a5 = addr[5]; a6 = addr[6]; a7 = addr[7]; ramSel8[7:0] = {8{ramSel}};
  //   sel0_8[7:0] = {8{sel0}}; sel1_8[7:0] = {8{sel1}}; sel2_8[7:0] = {8{sel2}}; sel3_8[7:0] = {8{sel3}};
  //   sel4_8[7:0] = {8{sel4}}; sel5_8[7:0] = {8{sel5}}; sel6_8[7:0] = {8{sel6}}; sel7_8[7:0] = {8{sel7}};
  //   sel8_8[7:0] = {8{sel8}}; sel9_8[7:0] = {8{sel9}}

  // Notes on the sheet:
  //   MEM stage: RAM 0x00-0x7F, reserved 0x80-0xEF, peripheral decode 0xF0-0xFF
endmodule

module memwb (
  input  clk,
  input  rst,
  input  v_d,
  input  regWrite_d,
  input  memRead,
  input  [2:0] dest_d,
  input  [7:0] alu,
  input  [7:0] memData,
  output v,
  output regWrite,
  output [2:0] dest,
  output [7:0] data
);

  wire [7:0] data_d;

  Register #(.width(1)) register_1 (.D(v_d), .en(1'b1), .Q(v), .clk(clk), .clr(rst));
  Register #(.width(1)) register_2 (.D(regWrite_d), .en(1'b1), .Q(regWrite), .clk(clk), .clr(rst));
  Register #(.width(3)) register_3 (.D(dest_d), .en(1'b1), .Q(dest), .clk(clk), .clr(rst));
  mux2_8 sel (.sel(memRead), .a(alu), .b(memData), .y(data_d));
  Register register_4 (.D(data_d), .en(1'b1), .Q(data), .clk(clk), .clr(rst));

  // Other names for the same wires on the sheet: alu_n[7:0] = alu

  // Notes on the sheet:
  //   MEM/WB register (load data or ALU result selected in MEM)
  //   sel  (mux2_8)
endmodule

module periph (
  input  clk,
  input  rst,
  input  wr_act,
  input  wr_disp,
  input  [7:0] wdata,
  output [7:0] act,
  output [7:0] disp,
  output valve,
  output heater,
  output motor_en,
  output motor_dir,
  output pump,
  output lock,
  output buzzer
);

  Register #(.width(7)) register_1 (.D(wdata[6:0]), .en(wr_act), .Q(act[6:0]), .clk(clk), .clr(rst));
  Register register_2 (.D(wdata), .en(wr_disp), .Q(disp), .clk(clk), .clr(rst));

  assign act[7] = 1'b0;
  assign buzzer = act[6];
  assign heater = act[1];
  assign lock = act[5];
  assign motor_dir = act[3];
  assign motor_en = act[2];
  assign pump = act[4];
  assign valve = act[0];

  // Other names for the same wires on the sheet: act7[6:0] = act[6:0]; act_d[6:0] = wdata[6:0]

  // Notes on the sheet:
  //   Actuator latch (ACT 0xF4) and DISPLAY register (0xF5)
endmodule

module eq8 (
  input  [7:0] a,
  input  [7:0] b,
  output eq
);

  wire [7:0] d;

  assign d = a ^ b;  // XOR_Gate xor_1, 8 bits wide
  zero8 z (.a(d), .z(eq));

  // Notes on the sheet:
  //   eq = 1 when a == b (8 bit)
  //   z  (zero8)
endmodule

module timer (
  input  clk,
  input  rst,
  input  wr_lim,
  input  wr_ctl,
  input  [7:0] wdata,
  output [7:0] count,
  output [7:0] limit,
  output [7:0] ctl,
  output [7:0] stat
);

  wire clr, cnt_en, eqL, hit, inc_cy, limIsZero, limNZ, m_or, match_d, nclr;
  wire [7:0] cnt_d, cnt_inc;

  or or_1 (cnt_en, clr, ctl[0]);
  not not_1 (limNZ, limIsZero);
  Register register_1 (.D(cnt_d), .en(cnt_en), .Q(count), .clk(clk), .clr(rst));
  and and_1 (hit, ctl[0], eqL, limNZ);
  and and_2 (clr, wr_ctl, wdata[1]);
  not not_2 (nclr, clr);
  or or_2 (m_or, stat[0], hit);
  Register register_2 (.D(wdata), .en(wr_lim), .Q(limit), .clk(clk), .clr(rst));
  and and_3 (match_d, m_or, nclr);
  add8 inc (.a(count), .b({8{1'b0}}), .cin(1'b1), .s(cnt_inc), .cout(inc_cy));
  Register #(.width(1)) register_3 (.D(wdata[0]), .en(wr_ctl), .Q(ctl[0]), .clk(clk), .clr(rst));
  Register #(.width(1)) register_4 (.D(match_d), .en(1'b1), .Q(stat[0]), .clk(clk), .clr(rst));
  eq8 cmp (.a(cnt_inc), .b(limit), .eq(eqL));
  zero8 limz (.a(limit), .z(limIsZero));
  assign cnt_d = cnt_inc & {8{nclr}};  // AND_Gate and_4, 8 bits wide

  assign ctl[7:1] = {7{1'b0}};
  assign stat[7:1] = {7{1'b0}};

  // Other names for the same wires on the sheet: en = ctl[0]; nclr8[7:0] = {8{nclr}}; match = stat[0]; w0 = wdata[0];
  //   w1 = wdata[1]; w2 = wdata[2]; w3 = wdata[3]; w4 = wdata[4]; w5 = wdata[5]; w6 = wdata[6]; w7 = wdata[7]

  // Notes on the sheet:
  //   Timer: COUNT, LIMIT, CTRL (EN, CLR), sticky MATCH
  //   inc  (add8)
  //   cmp  (eq8)
  //   limz  (zero8)
endmodule

module safety (
  input  clk,
  input  rst,
  input  cpu_motor_en,
  input  door_closed,
  input  start,
  output actual_motor_en,
  output trip
);

  wire door_open, hold, nmotor, nprev, nrearm, ntrip, rearm, set, start_prev, start_rise, trip_d;

  Register #(.width(1)) register_1 (.D(start), .en(1'b1), .Q(start_prev), .clk(clk), .clr(rst));
  and and_1 (rearm, nmotor, start_rise, door_closed);
  and and_2 (actual_motor_en, cpu_motor_en, door_closed, ntrip);
  not not_1 (nrearm, rearm);
  not not_2 (nprev, start_prev);
  and and_3 (hold, trip, nrearm);
  and and_4 (start_rise, start, nprev);
  or or_1 (trip_d, set, hold);
  not not_3 (door_open, door_closed);
  Register #(.width(1)) register_2 (.D(trip_d), .en(1'b1), .Q(trip), .clk(clk), .clr(rst));
  and and_5 (set, cpu_motor_en, door_open);
  not not_4 (ntrip, trip);
  not not_5 (nmotor, cpu_motor_en);

  // Notes on the sheet:
  //   Safety interlock: combinational door gate + TRIP latch
endmodule

module washing_pipeline (
  input  rst,
  input  START,
  input  [1:0] MODE,
  input  DOOR_CLOSED,
  input  [7:0] WATER_LEVEL,
  input  [7:0] TEMP,
  input  [7:0] DRUM_RPM,
  output VALVE_IN,
  output HEATER,
  output MOTOR_EN_CMD,
  output MOTOR_EN_ACTUAL,
  output MOTOR_DIR,
  output PUMP_OUT,
  output DOOR_LOCK,
  output BUZZER,
  output TRIP,
  output HALTED,
  output [7:0] DISPLAY,
  output [7:0] PC,
  output [7:0] TIMER_COUNT,
  output TIMER_MATCH,
  output STALL,
  output FLUSH,
  output IFID_V,
  output IDEX_V,
  output EXMEM_V,
  output MEMWB_V,
  output WR_ACT,
  output WR_DISP,
  output WR_TLIM,
  output WR_TCTL,
  output [15:0] IFID_IR,
  output [7:0] MEM_ADDR,
  output [7:0] MEM_WDATA
);

  wire clk, d_aluSrcImm, d_brNZ, d_brZ, d_halt, d_jmp, d_memRead, d_memWrite, d_regWrite, d_usesA, d_usesB,
       ex_aluSrcImm, ex_brNZ, ex_brZ, ex_halt, ex_jmp, ex_memRead, ex_memWrite, ex_regWrite, ex_usesA,
       ex_usesB, ex_v, haltEX, ifid_v_t, kill, mem_memRead, mem_memWrite, mem_regWrite, mem_v, redirect,
       stall_t, vnext, wb_regWrite, wb_v, wb_we, wr_act_t, wr_disp_t, wr_tctl_t, wr_tlim_t;
  wire [2:0] d_aluOp, d_fA, d_fB, ex_aluOp, ex_fA, ex_fB, mem_dest, wb_dest;
  wire [7:0] act, d_imm, ex_alu, ex_aval, ex_bval, ex_fwdA, ex_imm, mem_alu, mem_rdata, mem_stData, rf_a,
       rf_b, tctl, tlimit, wb_data;
  wire [7:1] tstat;
  wire [15:0] if_ir, ifid_ir_t;

  Clock u_CLK (.out(clk));
  buf buffer_1 (IFID_V, ifid_v_t);
  buf buffer_2 (WR_TCTL, wr_tctl_t);
  and and_1 (wb_we, wb_v, wb_regWrite);
  fetch IF (
    .clk(clk), .rst(rst), .redirect(redirect), .target(ex_imm), .stall(stall_t), .haltEX(haltEX), .pc(PC),
    .ir(if_ir), .halted(HALTED));
  execute EX (
    .aval(ex_aval), .bval(ex_bval), .imm(ex_imm), .fA(ex_fA), .fB(ex_fB), .aluOp(ex_aluOp), .usesA(ex_usesA),
    .usesB(ex_usesB), .aluSrcImm(ex_aluSrcImm), .brZ(ex_brZ), .brNZ(ex_brNZ), .jmp(ex_jmp), .halt(ex_halt),
    .v(ex_v), .exV(mem_v), .exRW(mem_regWrite), .exMR(mem_memRead), .exDest(mem_dest), .exAlu(mem_alu),
    .wbV(wb_v), .wbRW(wb_regWrite), .wbDest(wb_dest), .wbData(wb_data), .alu_out(ex_alu), .fwdA(ex_fwdA),
    .redirect(redirect), .haltEX(haltEX));
  memwb MEM_WB (
    .clk(clk), .rst(rst), .v_d(mem_v), .regWrite_d(mem_regWrite), .memRead(mem_memRead), .dest_d(mem_dest),
    .alu(mem_alu), .memData(mem_rdata), .v(wb_v), .regWrite(wb_regWrite), .dest(wb_dest), .data(wb_data));
  safety SAFE (
    .clk(clk), .rst(rst), .cpu_motor_en(MOTOR_EN_CMD), .door_closed(DOOR_CLOSED), .start(START),
    .actual_motor_en(MOTOR_EN_ACTUAL), .trip(TRIP));
  buf buffer_3 (IDEX_V, ex_v);
  assign IFID_IR = ifid_ir_t;  // Buffer buffer_4, 16 bits wide
  buf buffer_5 (EXMEM_V, mem_v);
  idex ID_EX (
    .clk(clk), .rst(rst), .vnext(vnext), .regWrite_d(d_regWrite), .memRead_d(d_memRead),
    .memWrite_d(d_memWrite), .aluSrcImm_d(d_aluSrcImm), .brZ_d(d_brZ), .brNZ_d(d_brNZ), .jmp_d(d_jmp),
    .halt_d(d_halt), .usesA_d(d_usesA), .usesB_d(d_usesB), .aluOp_d(d_aluOp), .fA_d(d_fA), .fB_d(d_fB),
    .imm_d(d_imm), .aval_d(rf_a), .bval_d(rf_b), .regWrite(ex_regWrite), .memRead(ex_memRead),
    .memWrite(ex_memWrite), .aluSrcImm(ex_aluSrcImm), .brZ(ex_brZ), .brNZ(ex_brNZ), .jmp(ex_jmp),
    .halt(ex_halt), .usesA(ex_usesA), .usesB(ex_usesB), .aluOp(ex_aluOp), .fA(ex_fA), .fB(ex_fB),
    .imm(ex_imm), .aval(ex_aval), .bval(ex_bval), .v(ex_v));
  assign MEM_ADDR = mem_alu;  // Buffer buffer_6, 8 bits wide
  ifid IF_ID (
    .clk(clk), .rst(rst), .hold(stall_t), .flush(kill), .halted(HALTED), .ir_in(if_ir), .v(ifid_v_t),
    .ir(ifid_ir_t));
  buf buffer_7 (MEMWB_V, wb_v);
  exmem EX_MEM (
    .clk(clk), .rst(rst), .v_d(ex_v), .regWrite_d(ex_regWrite), .memRead_d(ex_memRead),
    .memWrite_d(ex_memWrite), .dest_d(ex_fA), .alu_d(ex_alu), .stData_d(ex_fwdA), .v(mem_v),
    .regWrite(mem_regWrite), .memRead(mem_memRead), .memWrite(mem_memWrite), .dest(mem_dest), .alu(mem_alu),
    .stData(mem_stData));
  periph IO (
    .clk(clk), .rst(rst), .wr_act(wr_act_t), .wr_disp(wr_disp_t), .wdata(mem_stData), .act(act),
    .disp(DISPLAY), .valve(VALVE_IN), .heater(HEATER), .motor_en(MOTOR_EN_CMD), .motor_dir(MOTOR_DIR),
    .pump(PUMP_OUT), .lock(DOOR_LOCK), .buzzer(BUZZER));
  assign MEM_WDATA = mem_stData;  // Buffer buffer_8, 8 bits wide
  buf buffer_9 (WR_ACT, wr_act_t);
  decode ID (
    .ir(ifid_ir_t), .regWrite(d_regWrite), .memRead(d_memRead), .memWrite(d_memWrite),
    .aluSrcImm(d_aluSrcImm), .brZ(d_brZ), .brNZ(d_brNZ), .jmp(d_jmp), .halt(d_halt), .usesA(d_usesA),
    .usesB(d_usesB), .aluOp(d_aluOp), .fA(d_fA), .fB(d_fB), .imm(d_imm));
  hazard HZ (
    .idexV(ex_v), .idexMemRead(ex_memRead), .ifidV(ifid_v_t), .usesA(d_usesA), .usesB(d_usesB),
    .redirect(redirect), .haltEX(haltEX), .idexDest(ex_fA), .fA(d_fA), .fB(d_fB), .stall(stall_t),
    .kill(kill), .vnext(vnext));
  buf buffer_10 (WR_DISP, wr_disp_t);
  timer TMR (
    .clk(clk), .rst(rst), .wr_lim(wr_tlim_t), .wr_ctl(wr_tctl_t), .wdata(mem_stData), .count(TIMER_COUNT),
    .limit(tlimit), .ctl(tctl), .stat({tstat, TIMER_MATCH}));
  mem_stage MEM (
    .v(mem_v), .memRead(mem_memRead), .memWrite(mem_memWrite), .addr(mem_alu), .wdata(mem_stData), .clk(clk),
    .rd_in_ctrl({3'b000, TRIP, DOOR_CLOSED, MODE, START}), .rd_water(WATER_LEVEL), .rd_temp(TEMP),
    .rd_rpm(DRUM_RPM), .rd_act(act), .rd_disp(DISPLAY), .rd_tcount(TIMER_COUNT), .rd_tlimit(tlimit),
    .rd_tctl(tctl), .rd_tstat({tstat, TIMER_MATCH}), .rdata(mem_rdata), .wr_act(wr_act_t),
    .wr_disp(wr_disp_t), .wr_tlim(wr_tlim_t), .wr_tctl(wr_tctl_t));
  buf buffer_11 (STALL, stall_t);
  buf buffer_12 (WR_TLIM, wr_tlim_t);
  regfile RF (.clk(clk), .raA(d_fA), .raB(d_fB), .wEn(wb_we), .wAddr(wb_dest), .wData(wb_data), .rdA(rf_a), .rdB(rf_b));
  buf buffer_13 (FLUSH, kill);

  // Other names for the same wires on the sheet: in_ctrl[4:0] = {TRIP, DOOR_CLOSED, MODE, START};
  //   tstat[0] = TIMER_MATCH

  // Notes on the sheet:
  //   Five-stage pipelined washing-machine controller (top level)
  //   SAFE  (safety)
  //   IF  (fetch)
  //   EX  (execute)
  //   MEM_WB  (memwb)
  //   ID_EX  (idex)
  //   IF_ID  (ifid)
  //   EX_MEM  (exmem)
  //   IO  (periph)
  //   ID  (decode)
  //   HZ  (hazard)
  //   TMR  (timer)
  //   MEM  (mem_stage)
  //   RF  (regfile)
endmodule
